# Fritzing sketch 3color_arduino (saved by Fritzing 0.9.3b)
breadboards: 1

parts:
  부품1 = Arduino Uno (Rev3)
  R1 = Resistor [tolerance=±5% resistance=330 package=THT]
  R2 = Resistor [tolerance=±5% resistance=330 package=THT]
  R3 = Resistor [tolerance=±5% resistance=330 package=THT]
  LED1 = LED - 5mm [color="Green (560nm)" package="5 mm [THT]"]
  LED2 = LED - 5mm [color="Yellow (592nm)" package="5 mm [THT]"]
  LED3 = LED - 5mm [color="Red (635nm)" package="5 mm [THT]"]

nets:
  N1: 부품1.D8, R3.Pin_0
  N2: 부품1.D10_PWM/SS, R2.Pin_0
  N3: 부품1.D12/MISO, R1.Pin_0
  N4: 부품1.GND, LED1.anode, LED2.anode, LED3.anode
  N5: R1.Pin_1, LED1.cathode
  N6: R2.Pin_1, LED2.cathode
  N7: R3.Pin_1, LED3.cathode
